# Fritzing sketch wifi_回路図 (saved by Fritzing 0.9.6b)
circuit board: 5.26954cm x 4.53328cm
breadboards: 1

parts:
  VCC1 = Battery
  Raspberry_Pi_1 = Raspberry Pi 3 [part_number=RPI-3-V1.2]
  IC1 = L293D [package=THT]
  vol = male pin header, 4 pins [form="♂ (male)"]
  motter_setting_2 = male pin header, 3 pins [form="♂ (male)"]
  motter_1 = male pin header, 2 pins [form="♂ (male)"]
  motter_2 = male pin header, 2 pins [form="♂ (male)"]
  M1 = DC Motor
  M2 = DC Motor
  moter_setting_1 = male pin header, 3 pins [form="♂ (male)"]
  J1 = male pin header, 1 pin [form="♂ (male)"]  # not connected
  J2 = male pin header, 1 pin [form="♂ (male)"]  # not connected
  J3 = male pin header, 1 pin [form="♂ (male)"]  # not connected
  J4 = male pin header, 1 pin [form="♂ (male)"]  # not connected
  J5 = male pin header, 1 pin [form="♂ (male)"]  # not connected
  J7 = male pin header, 1 pin [form="♂ (male)"]  # not connected
  J8 = male pin header, 1 pin [form="♂ (male)"]  # not connected
  J9 = male pin header, 1 pin [form="♂ (male)"]  # not connected
  C1 = Ceramic Capacitor [capacitance=100nF voltage=35V package="100 mil [THT, multilayer]"]
  C2 = Ceramic Capacitor [capacitance=100nF voltage=35V package="100 mil [THT, multilayer]"]

nets:
  N1: VCC1.-, Raspberry_Pi_1.GND, IC1.0V, vol.pin3, vol.pin4, C1.0, C2.0
  N2: VCC1.+, IC1.+Vmotor, vol.pin1, C1.1
  N3: Raspberry_Pi_1.GIPO17, IC1.In_2, moter_setting_1.pin1
  N4: Raspberry_Pi_1.GIPO27, IC1.In_1, moter_setting_1.pin2
  N5: Raspberry_Pi_1.GIPO22, IC1.Enable_1, moter_setting_1.pin3
  N6: Raspberry_Pi_1.GIPO5, IC1.In_4, motter_setting_2.pin1
  N7: Raspberry_Pi_1.GIPO6, IC1.Out_3_(_Controlled_by_Enable_2_), motter_setting_2.pin2
  N8: Raspberry_Pi_1.GIPO13, IC1.Enable_2, motter_setting_2.pin3
  N9: Raspberry_Pi_1.5V, IC1.+V, vol.pin2, C2.1
  N10: IC1.Out_1_(_Controlled_by_Enable_1_), motter_1.pin1, M1.pin_2
  N11: IC1.Out_2_(_Controlled_by_Enable_1_), motter_1.pin2, M1.pin_1
  N12: IC1.In_3, motter_2.pin2, M2.pin_1
  N13: IC1.Out_4_(_Controlled_by_Enable_2_), motter_2.pin1, M2.pin_2
